# Fritzing sketch schematic (saved by Fritzing 1.0.4)
breadboards: 1

parts:
  A1 = Raspberry Pi 5  # not connected
  L298N1 = L298N DC motor driver
  M3 = DC Motor [voltage_(max)=6V voltage_(min)=3V]
  M4 = DC Motor [voltage_(max)=6V voltage_(min)=3V]
  Part1 = Arduino Uno (Rev3) - ICSP
  GY1 = MPU-6050 Board GY-521 [form="♀ (female)" package=THT]
  A2 = tf-luna lidar
  M5 = bb-usb-cable [package=THT]  # not connected
  M6 = RioRand LM2596
  M7 = bb-usb-cable [package=THT]  # not connected
  Mod1 = generic-ac-power-supply [package=THT]

nets:
  N1: L298N1.OUT1, M3.pin_2
  N2: L298N1.OUT2, M3.pin_1
  N3: L298N1.OUT3, M4.pin_2
  N4: L298N1.OUT4, M4.pin_1
  N5: L298N1.12V, M6.Pin_2, Mod1.pin3#3
  GND: L298N1.GND, Part1.GND, GY1.pin2, A2.Pin_4, A2.Pin_5, M6.Pin_1, Mod1.pin3#2
  5V: L298N1.5V, Part1.5V, GY1.pin1, A2.Pin_1
  N6: L298N1.ENA, Part1.D9_PWM
  N7: L298N1.ENB, Part1.D10_PWM/SS
  N8: L298N1.IN1, Part1.D2
  N9: L298N1.IN2, Part1.D3_PWM
  N10: L298N1.IN3, Part1.D4
  N11: L298N1.IN4, Part1.D5_PWM
  N12: Part1.A4/SDA, GY1.pin4, A2.Pin_2
  N13: Part1.A5/SCL, GY1.pin3, A2.Pin_3

custom parts:
  Raspberry Pi 5: The RPi5, a faster version of the awesome Raspberry Pi4B ARM Board with 40 pin gpio.
  L298N DC motor driver: 2x DC motor driver with 78M05 positive voltage regulator (7..35 V) L298N: max 46 V, 2 A Set 5 V Enable jumper to enable 5 V regultor (needed for the L298N) and +5 V output at screw terminal or supply external +5 V at screw terminal Set ENA and/or ENB to +5 V to enable motor permanently or supply ENA and/or ENB with PWM signal IN1 and IN2 set rotation directory for motor A (OUT1/OUT2) IN2 and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
  MPU-6050 Board GY-521: Acelerometro y Giroscopio MPU-6050 Board GY-521
  tf-luna lidar: TF-Luna is using Time of Flight (TOF) principle to measure distance, and it periodically emits near infrared modulated wave.
  bb-usb-cable: Breadboard only, no connectors USB cable for the Raspberry PIs.
  generic-ac-power-supply: Generic ac power supply module. Use as is, or customize the svgs to fit your particular device (as they are all different.) Provides AC input and single DC output. PCB is generic and will need modifications if you intend to do a pcb mount.
